# Fritzing sketch RGBWController (saved by Fritzing 0.9.3b)
breadboards: 1

parts:
  ESP-12F_w/breakout = Gizwits WiFi Witty ESP-12F
  S1_-_FLASH = SPST Switch [package=switch-spdt-smd]
  S2_-_RESET = SWITCH-MOMENTARY-2 [package=tactile_switch_tall]
  R1 = Resistor [tolerance=±5% resistance=10k package="0402 [SMD]"]
  Part3 = I2C level shifter bidirectional
  U1 = V_REG_LD1117VXX [package=78xxl]
  J1 = Camdenboss CTB0158-7 [part_number=CTB0158-7 package=THT]
  J2 = Camdenboss CTB0158-3 [part_number=CTB0158-3 package=THT]

nets:
  N1: ESP-12F_w/breakout.REST, ESP-12F_w/breakout.GPIO16, S2_-_RESET.1
  N2: ESP-12F_w/breakout.CH_PD, ESP-12F_w/breakout.VCC, R1.Pin_1, Part3.LV, U1.OUT
  N3: ESP-12F_w/breakout.GPIO14, Part3.LV4
  N4: ESP-12F_w/breakout.GPIO12, Part3.LV3
  N5: ESP-12F_w/breakout.GPIO13, Part3.LV2
  GND: ESP-12F_w/breakout.GND, ESP-12F_w/breakout.GPIO15, S1_-_FLASH.S, S2_-_RESET.2, U1.GND, J1.pin6, J2.pin1
  N6: ESP-12F_w/breakout.GPIO2, Part3.LV1
  N7: ESP-12F_w/breakout.GPIO0, S1_-_FLASH.P
  N8: ESP-12F_w/breakout.RXD, J2.pin2
  N9: ESP-12F_w/breakout.TXD, J2.pin3
  N10: S1_-_FLASH.O, R1.Pin_0
  N11: Part3.HV1, J1.pin1
  N12: Part3.HV2, J1.pin2
  N13: Part3.HV, J1.pin5
  N14: Part3.HV3, J1.pin3
  N15: Part3.HV4, J1.pin4
  N16: U1.IN, J1.pin7

notes:
  White
  Blue
  Red
  Green
  +5V
  GND
  +12V
