# Fritzing sketch RGBWPower (saved by Fritzing 0.9.3b)
breadboards: 1

parts:
  J2 = Camdenboss CTB0158-7 [part_number=CTB0158-7 package=THT]
  J3 = Power Jack [package=power_jack_smd]
  Q1 = MOSFET-NCHANNEL [package=to220v]
  J4 = Camdenboss CTB0158-5 [part_number=CTB0158-5 package=THT]
  Q2 = MOSFET-NCHANNEL [package=to220v]
  Q3 = MOSFET-NCHANNEL [package=to220v]
  Q4 = MOSFET-NCHANNEL [package=to220v]
  U2 = Voltage Regulator [package=78xxl]

nets:
  N1: J2.terminal_1, Q1.G
  N2: J2.terminal_2, Q2.G
  N3: J2.terminal_3, Q3.G
  N4: J2.terminal_4, Q4.G
  N5: J2.terminal_5, U2.OUT
  N6: J2.terminal_6, J3.GND, Q1.S, Q2.S, Q3.S, Q4.S
  N7: J2.terminal_7, J3.PWR, J4.pin5, U2.IN
  N8: Q1.D, J4.pin1
  N9: J4.pin2, Q2.D
  N10: J4.pin3, Q3.D
  N11: J4.pin4, Q4.D

notes:
  White
  Blue
  Red
  Green
  +5V
  GND
  +12V
  White
  Blue
  Red
  Green
  +12V
